# Fritzing sketch midi-vaderswrapper (saved by Fritzing 0.9.6b)
breadboards: 1

parts:
  R1 = Rotary Potentiometer (Large) [maximum_resistance=10kΩ package=THT]
  R2 = Rotary Potentiometer (Large) [maximum_resistance=10kΩ package=THT]
  R3 = Rotary Potentiometer (Large) [maximum_resistance=10kΩ package=THT]
  R5 = Rotary Potentiometer (Large) [maximum_resistance=10kΩ package=THT]
  R6 = Rotary Potentiometer (Large) [maximum_resistance=10kΩ package=THT]
  R7 = Rotary Potentiometer (Large) [maximum_resistance=10kΩ package=THT]
  Pro_Micro1 = SparkFun Pro Micro
  Mod1 = KY-023 Dual Axis Joystick Module [package="Breakout board"]

nets:
  GND: R1.leg1, R2.leg1, R3.leg1, R5.leg2, R6.leg2, R7.leg2, Pro_Micro1.GND, Mod1.GND
  N1: R1.wiper, Pro_Micro1.A0
  5V: R1.leg2, R2.leg2, R3.leg2, R5.leg1, R6.leg1, R7.leg1, Pro_Micro1.VCC, Mod1.+5V
  N2: R2.wiper, Pro_Micro1.A1
  N3: R3.wiper, Pro_Micro1.A2
  N4: R5.wiper, Pro_Micro1.10
  N5: R6.wiper, Pro_Micro1.9
  N6: R7.wiper, Pro_Micro1.8
  N7: Pro_Micro1.4, Mod1.SW
  N8: Pro_Micro1.6, Mod1.VRy
  N9: Pro_Micro1.A3, Mod1.VRx

custom parts:
  SparkFun Pro Micro: The Pro Micro is similar to the Pro Mini except with an ATmega32U4 on board. The USB transceiver inside the 32U4 allows us to add USB connectivity on-board and do away with bulky external USB interface. Based on: https://github.com/unorthodox-engineers/unorthodox-arduino/blob/master/Unorthodox/fritzing/parts/Pro%20Micro.fzpz
  KY-023 Dual Axis Joystick Module: KY-023 Dual-Axis Joystick Module.

// code stored in the sketch: midi-gorkon.ino
#include <Control_Surface.h>
#include <EEPROM.h>

// Number of encoders (XY = 2 encoders)
#define ENC_NB 8

USBMIDI_Interface midi;  // Instantiate a MIDI Interface to use

uint8_t default_enc_mcc[] = {MIDI_CC::Sound_Controller_2, MIDI_CC::Sound_Controller_4, MIDI_CC::Portamento_Time,  MIDI_CC::Effects_1, 
                             MIDI_CC::Sound_Controller_5, MIDI_CC::Sound_Controller_4, MIDI_CC::Effects_4,        MIDI_CC::Pan};

CCPotentiometer enc[] = {
  { A10, 0 }, { A9, 0 }, { A8, 0 }, { A7, 0 },
  { A0,  0 }, { A1, 0 }, { A2, 0 }, { A3, 0 }
};

enum
{
  PATCH_REQ, // In:  Request for current configuration
  PATCH_STS, // Out: Send configuration
  PATCH_CMD, // In:  New patch command
  SAVE_CMD,  // In:  Save current configuration command
  RESET_CMD  // In:  Restore default configuration
};

typedef union
{
  struct msg
  {
    uint8_t syx_hdr; // 0xF0
    uint8_t msg_idx;
    uint8_t enc_mcc[ENC_NB];
    uint8_t syx_ftr; // 0xF7
  } sts;
  uint8_t array[sizeof(struct msg)];
} patch_sts_u;


typedef struct
{
  uint8_t syx_hdr; // 0xF0
  uint8_t msg_idx;
  uint8_t enc_idx;
  uint8_t enc_mcc;
  uint8_t syx_ftr; // 0xF7
} patch_cmd_t;

void sendPatchStatus()
{
  patch_sts_u sts;
  sts.sts.syx_hdr = 0xF0;
  sts.sts.syx_ftr = 0xF7;
  sts.sts.msg_idx = PATCH_STS;
  
  for (int i = 0; i < ENC_NB; i++)
    sts.sts.enc_mcc[i] = enc[i].getAddress().getAddress();

  midi.sendSysEx(sts.array);
}

void updatePatch(const uint8_t* array, unsigned size)
{
  if (size == sizeof(patch_cmd_t))
  {
    patch_cmd_t* patch = (patch_cmd_t*)array;
    if ((patch->enc_idx < ENC_NB) && (patch->enc_mcc <= 127))
      enc[patch->enc_idx].setAddress(patch->enc_mcc);
  }
}

void saveConfig()
{
  for (int i = 0; i < ENC_NB; i++)
    EEPROM.update(i, enc[i].getAddress().getAddress());
}

void restoreConfig()
{
  for (int i = 0; i < ENC_NB; i++)
  {
    uint8_t value = EEPROM.read(i);
    if (value <= 127)
      enc[i].setAddress(value);
    else
      enc[i].setAddress(default_enc_mcc[i]);
  }
}

void resetConfig()
{
  for (int i = 0; i < ENC_NB; i++)
    enc[i].setAddress(default_enc_mcc[i]);
}

// Custom MIDI callback that prints incoming SysEx messages.
struct MyMIDI_Callbacks : MIDI_Callbacks {
 
  // This callback function is called when a SysEx message is received.
  void onSysExMessage(MIDI_Interface &, SysExMessage sysex) override {
#ifdef DEBUG
    // Print the message
    Serial << F("Received SysEx message: ")         //
           << AH::HexDump(sysex.data, sysex.length) //
           << F(" on cable ") << sysex.cable.getOneBased() << endl;
#endif

    if (sysex.length < 1) return;
    switch (sysex.data[1])
    {
      case PATCH_REQ:
        sendPatchStatus();
        break;
      case PATCH_CMD:
        updatePatch(sysex.data, sysex.length);
        break;
      case SAVE_CMD:
        saveConfig();
        break;
      case RESET_CMD:
        resetConfig();
        break;
      default:
        break;
    }
  }
} callback {};

void setup() {
  
  restoreConfig();
  
  Control_Surface.begin();  // Initialize the Control Surface
  midi.begin();
  midi.setCallbacks(callback);
}

void loop() {
  Control_Surface.loop();  // Update the Control Surface
  midi.update();
}

// code stored in the sketch: midi-octopot.ino
#include <MIDIUSB.h>
#include <MIDIUSB_Defs.h>

enum {
    MIDI_CC_PORTAMENTO_TIME             = 0x05,
    MIDI_CC_VOLUME                      = 0x07,
    MIDI_CC_PAN_MSB                     = 0x0A,

    MIDI_CC_SOUND_CONTROLLER_2          = 0x47, // Timbre/Harmonic Intensity
    MIDI_CC_SOUND_CONTROLLER_3          = 0x48, // Release Time
    MIDI_CC_SOUND_CONTROLLER_4          = 0x49, // Attack Time
    MIDI_CC_SOUND_CONTROLLER_5          = 0x4A, // Brightness
    MIDI_CC_EFFECTS_1_DEPTH             = 0x5B, // Reverb amount
    MIDI_CC_EFFECTS_4_DEPTH             = 0x5F, // Detune amount
};

#define MIDI_CHANNEL 0
#define POT_NB 8

byte pot_pin[] = {A0,  A1, A2, A3,
                  A10, A9, A8, A7};

byte pot_mcc[] = {MIDI_CC_SOUND_CONTROLLER_2, MIDI_CC_SOUND_CONTROLLER_3, MIDI_CC_PORTAMENTO_TIME, MIDI_CC_EFFECTS_1_DEPTH, 
                  MIDI_CC_SOUND_CONTROLLER_5, MIDI_CC_SOUND_CONTROLLER_4, MIDI_CC_EFFECTS_4_DEPTH, MIDI_CC_PAN_MSB};

byte pot_val[] = {0, 0, 0, 0, 0, 0, 0, 0};

void controlChange(byte channel, byte control, byte value) {

  midiEventPacket_t event = {0x0B, 0xB0 | channel, control, value};

  MidiUSB.sendMIDI(event);
  MidiUSB.flush();
}

void setup() {
  // put your setup code here, to run once:
   Serial.begin(115200);
}

void loop() {
  // put your main code here, to run repeatedly:
  for (byte i = 0; i < POT_NB; i++)
  {
    byte val = analogRead(pot_pin[i]) / 8;
    if (val != pot_val[i])
    {
      pot_val[i] = val;
      controlChange(MIDI_CHANNEL, pot_mcc[i], pot_val[i]);
    }
    char buf[5];
    sprintf(buf, "%3d ", (int)pot_val[i]);
    Serial.print(buf);
  }
  Serial.println();
}
